# Fritzing sketch circuit (saved by Fritzing 0.9.3b)
breadboards: 1

parts:
  BAT1 = BC9VPC [package=bc9vpc]  # not connected
  J1 = Basic Servo
  J2 = Basic Servo
  J3 = Basic Servo
  Raspberry_Pi_1 = Raspberry Pi 3 [part_number=RPI-3-V1.2]

nets:
  GND: J1.gnd, J2.gnd, J3.gnd, Raspberry_Pi_1.GND
  VCC: J1.vcc, J2.vcc, J3.vcc
  N1: J1.pulse, Raspberry_Pi_1.GIPO4
  N2: J2.pulse, Raspberry_Pi_1.GIPO17
  N3: J3.pulse, Raspberry_Pi_1.GIPO27
